// Digital circuit assembler.dig as structural Verilog
module assembler (
  input  mode,
  input  [7:0] value,
  input  [1:0] dest,
  input  [1:0] src,
  input  tworeg,
  input  add,
  input  move,
  input  jump,
  output [15:0] instr,
  output store
);

  wire priorityencoder_1_any;

  PriorityEncoder #(.Selector_Bits(3)) priorityencoder_1 (
    .in0(add), .in1(1'b0), .in2(1'b0), .in3(1'b0), .in4(1'b0), .in5(1'b0), .in6(move), .in7(jump),
    .num(instr[3:1]), .any(priorityencoder_1_any));
  and and_1 (store, priorityencoder_1_any, mode);

  assign {instr[15:4], instr[0]} = {value, src, dest, tworeg};

  // Notes on the sheet:
  //   mode: default -1
  //   add: default 1
  //   move: default -1
  //   jump: default -1
endmodule
