// Digital circuit fecthc_counter.dig as structural Verilog
module fecthc_counter (
  input  [15:0] instr_i,
  input  clock,
  input  [15:0] value,
  input  jump,
  output [15:0] instr_0,
  output [3:0] PC
);

  CounterPreset #(.Bits(4), .isProgramCounter("true")) u_PC (
    .en(1'b1), .C(clock), .dir(1'b0), .in(value[3:0]), .ld(jump), .clr(1'b0), .out(PC));  // open: ovf

  assign instr_0 = instr_i;
endmodule
