// Digital circuit hexdisplay.dig as structural Verilog
module hexdisplay (
  input  E,
  input  [15:0] V,
  output [3:0] D1,
  output [3:0] D2,
  output [3:0] D3,
  output [3:0] D4,
  output P1,
  output P2,
  output P3,
  output P4
);

  assign D1 = E ? V[15:12] : 4'bz;  // Driver driver_1
  assign D2 = E ? V[11:8] : 4'bz;  // Driver driver_2
  assign D3 = E ? V[7:4] : 4'bz;  // Driver driver_3
  assign D4 = E ? V[3:0] : 4'bz;  // Driver driver_4

  assign P1 = 1'b0;
  assign P2 = 1'b0;
  assign P3 = 1'b0;
  assign P4 = 1'b0;
endmodule
