// Digital circuit multiple_adder.dig as structural Verilog
module multiple_adder (
  input  [15:0] A,
  input  [7:0] SD,
  output [15:0] r0,
  output [15:0] r1,
  output [15:0] r2,
  output [15:0] r3,
  output [15:0] B,
  output [1:0] rd,
  output [15:0] A_2,
  output [1:0] rs
);

  wire button_1_out, button_2_out;
  wire [1:0] PC_out;
  wire [15:0] execute_1_p3;
  wire [31:0] PROGRAM_d;

  Button button_1 (.out(button_1_out));
  Button button_2 (.out(button_2_out));
  Counter #(.Bits(2)) PC (.en(1'b1), .C(button_2_out), .clr(1'b0), .out(PC_out));  // open: ovf
  EEPROMDualPort #(.Bits(32)) PROGRAM (
    .A(PC_out), .Din({{8{1'b0}}, SD, A}), .str(1'b1), .C(button_1_out), .ld(1'b1), .D(PROGRAM_d));
  // decoder decoder_1: pin names not known; wires that end beside it: PROGRAM_d, A_2, rs, rd
  // execute execute_1: pin names not known; wires that end beside it: A_2, B, execute_1_p3, B, r0, r1, r2, r3
  reg_file reg_file_1 (
    .RS(rs), .rd(rd), .result(execute_1_p3), .clock(button_2_out), .rsval(B));  // open: rdval, R0, R1, R2, R3

  // Other names for the same wires on the sheet: A_t[15:0] = A_2

  // Notes on the sheet:
  //   A: default 1
  //   SD: default 1
  //   contents of PROGRAM (hex, n*v repeats v):
  //   10001,120002,230003,300004
  //   R1
  //   =
  //   +
  //   R0
  //   (
  //   )
endmodule
